# Fritzing sketch C2_ButtonLED (saved by Fritzing 0.9.0b)
breadboards: 1

parts:
  Part1 = Arduino Mega 2560 (Rev3)
  LED4 = LED - 3mm [color="Green (555nm)" package="3 mm [THT]"]
  R1 = Resistor [package="2010 [SMD]"]
  S4 = Momentary Switch [package=ksa_sealed_tac_switch]
  R3 = Resistor [tolerance=±5% resistance=10k package=THT]

nets:
  N1: Part1.D21/SCL, S4.2, R3.Pin_1
  N2: Part1.GND, R1.Pin_0, S4.4
  N3: Part1.5V, R3.Pin_0
  N4: Part1.D2_PWM, LED4.anode
  N5: LED4.cathode, R1.Pin_1
