# Fritzing sketch Scratch1_3b (saved by Fritzing 0.9.1b)
breadboards: 1
perfboards: 1

parts:
  Part1 = Arduino Mega 2560 (Rev3)
  CC1 = Adafruit CC3000 Shield for Arduino
  S3 = Momentary Switch [package=ksa_sealed_tac_switch]
  LED4 = LED - 3mm [color="Green (555nm)" package="3 mm [THT]"]
  LED5 = RGB LED (com. cathode, rgb) [color="Green (555nm)" package="5 mm [THT]"]
  R1 = Resistor [package="2010 [SMD]"]
  R2 = Resistor [tolerance=±5% resistance=10k package=THT]
  R3 = Resistor [package="2010 [SMD]"]
  R4 = Resistor [package="2010 [SMD]"]
  R5 = Resistor [package="2010 [SMD]"]
  R6 = Rotary Potentiometer (Small) [maximum_resistance=100kΩ package=THT]
  R7 = PHOTOCELL [package=photocell]
  R8 = Resistor [tolerance=±5% resistance=10k package=THT]
  T1 = TMP36 Temperature Sensor [package="TO92 [THT]"]
  U1 = 7-SEGMENT-4DIGIT [package=7-segment-4digit-5641]  # not connected
  U2 = 7-SEGMENT-4DIGIT [package=7-segment-4digit-5641]  # not connected
  J1 = Basic Servo

nets:
  N1: Part1.A8, R7.P$1, R8.Pin_0
  N2: Part1.A9, T1.Vout
  N3: Part1.A0, CC1.A0
  N4: Part1.A1, CC1.A1
  N5: Part1.A2, CC1.A2
  N6: Part1.A3, CC1.A3
  N7: Part1.A4, CC1.A4
  N8: Part1.A5, CC1.A5, R6.wiper
  N9: Part1.D21/SCL, Part1.SCL, CC1.SCL, S3.2, R2.Pin_1
  N10: Part1.D20/SDA, Part1.SDA, CC1.SDA
  N11: Part1.AREF, CC1.AREF
  GND: Part1.GND, CC1.GND, S3.4, R1.Pin_0, R6.leg1, R8.Pin_1, T1.GND, J1.gnd
  N12: Part1.D13_PWM, CC1.D13
  N13: Part1.D12_PWM, CC1.D12
  N14: Part1.D11_PWM, CC1.D11
  N15: Part1.D10_PWM, CC1.D10
  N16: Part1.D9_PWM, CC1.D9
  N17: Part1.D8_PWM, CC1.D8
  N18: Part1.IOREF#254, CC1.NC
  N19: Part1.IOREF#255, CC1.IOr
  N20: Part1.RESET, CC1.RST
  N21: Part1.3V3, CC1.3V
  5V: Part1.5V, CC1.5V, R2.Pin_0, R6.leg2, R7.P$2, T1.+Vs, J1.vcc
  VIN: Part1.VIN, CC1.VIN
  N22: Part1.D0_RX0, CC1.D0
  N23: Part1.D1_TX0, CC1.D1
  N24: Part1.D2_PWM, CC1.D2, LED4.anode
  N25: Part1.D3_PWM, CC1.D3
  N26: Part1.D4_PWM, CC1.D4
  N27: Part1.D5_PWM, CC1.D5
  N28: Part1.D6_PWM, CC1.D6
  N29: Part1.D7_PWM, CC1.D7
  N30: Part1.D23, J1.pulse
  N31: Part1.D44, R3.Pin_0
  N32: Part1.D45, R4.Pin_0
  N33: Part1.D46, R5.Pin_0
  N34: S3.3, LED5.common_cathode
  N35: LED4.cathode, R1.Pin_1
  N36: LED5.red_anode, R3.Pin_1
  N37: LED5.green_anode, R4.Pin_1
  N38: LED5.blue_anode, R5.Pin_1

notes:
  LED flat this side

custom parts:
  7-SEGMENT-4DIGIT: if you need make parts, send me e-mail and write. Price 1 part=0.9 WMZ (http://www.wmtransfer.com/) ~ 0.9 Euro
