# Fritzing sketch 1b_Blink+Button+Pot+LED+7Seg+photocell+buzzer (saved by Fritzing 0.9.1b)
breadboards: 1
perfboards: 1

parts:
  Part1 = Arduino Mega 2560 (Rev3)
  CC1 = Adafruit CC3000 Shield for Arduino
  LED4 = LED - 3mm [color="Green (555nm)" package="3 mm [THT]"]
  R1 = Resistor [package="2010 [SMD]"]
  S4 = Momentary Switch [package=ksa_sealed_tac_switch]
  R3 = Resistor [tolerance=±5% resistance=10k package=THT]
  POT3 = Breadboard Trimpot
  R6 = Resistor [package="2010 [SMD]"]
  R7 = Resistor [package="2010 [SMD]"]
  R8 = Resistor [package="2010 [SMD]"]
  LED8 = RGB LED (com. cathode, rgb) [color="Green (555nm)" package="5 mm [THT]"]
  U3 = 7-SEGMENT-4DIGIT [package=7-segment-4digit-5641]  # not connected
  U4 = 7-SEGMENT-4DIGIT [package=7-segment-4digit-5641]  # not connected
  R9 = PHOTOCELL [package=photocell]
  R10 = Resistor [tolerance=±5% resistance=10k package=THT]
  J3 = Piezo Speaker

nets:
  N1: Part1.A8, R9.P$2, R10.Pin_0
  N2: Part1.A0, CC1.A0
  N3: Part1.A1, CC1.A1
  N4: Part1.A2, CC1.A2
  N5: Part1.A3, CC1.A3
  N6: Part1.A4, CC1.A4
  N7: Part1.A5, CC1.A5, POT3.PIN2
  N8: Part1.D21/SCL, Part1.SCL, CC1.SCL, S4.2, R3.Pin_1
  N9: Part1.D20/SDA, Part1.SDA, CC1.SDA
  N10: Part1.AREF, CC1.AREF
  GND: Part1.GND, CC1.GND, R1.Pin_0, S4.4, POT3.PIN1, R10.Pin_1, J3.pin1
  N11: Part1.D13_PWM, CC1.D13
  N12: Part1.D12_PWM, CC1.D12
  N13: Part1.D11_PWM, CC1.D11
  N14: Part1.D10_PWM, CC1.D10
  N15: Part1.D9_PWM, CC1.D9
  N16: Part1.D8_PWM, CC1.D8
  N17: Part1.IOREF#254, CC1.NC
  N18: Part1.IOREF#255, CC1.IOr
  N19: Part1.RESET, CC1.RST
  N20: Part1.3V3, CC1.3V
  5V: Part1.5V, CC1.5V, R3.Pin_0, POT3.PIN3, R9.P$1
  VIN: Part1.VIN, CC1.VIN
  N21: Part1.D0_RX0, CC1.D0
  N22: Part1.D1_TX0, CC1.D1, LED4.anode
  N23: Part1.D2_PWM, CC1.D2
  N24: Part1.D3_PWM, CC1.D3
  N25: Part1.D4_PWM, CC1.D4
  N26: Part1.D5_PWM, CC1.D5
  N27: Part1.D6_PWM, CC1.D6
  N28: Part1.D7_PWM, CC1.D7
  N29: Part1.D34, J3.pin2
  N30: Part1.D44, R8.Pin_0
  N31: Part1.D45, R7.Pin_0
  N32: Part1.D46, R6.Pin_0
  N33: LED4.cathode, R1.Pin_1
  N34: S4.3, LED8.common_cathode
  N35: R6.Pin_1, LED8.blue_anode
  N36: R7.Pin_1, LED8.green_anode
  N37: R8.Pin_1, LED8.red_anode

custom parts:
  7-SEGMENT-4DIGIT: if you need make parts, send me e-mail and write. Price 1 part=0.9 WMZ (http://www.wmtransfer.com/) ~ 0.9 Euro
