# Fritzing sketch C1_Blink (saved by Fritzing 0.9.2b)
breadboards: 1

parts:
  Part1 = Arduino Mega 2560 (Rev3)
  LED4 = LED - 3mm [color="Green (555nm)" package="3 mm [THT]"]
  R1 = Resistor [tolerance=±5% resistance=220 package="2010 [SMD]"]

nets:
  N1: Part1.GND, R1.Pin_0
  N2: Part1.D2_PWM, LED4.anode
  N3: LED4.cathode, R1.Pin_1
