# Fritzing sketch C3_PotBrightness (saved by Fritzing 0.9.2b)
breadboards: 1

parts:
  Part1 = Arduino Mega 2560 (Rev3)
  LED4 = LED - 3mm [color="Green (555nm)" package="3 mm [THT]"]
  S4 = Momentary Switch [package=ksa_sealed_tac_switch]
  R3 = Resistor [tolerance=±5% resistance=10k package=THT]
  POT3 = Breadboard Trimpot
  R1 = Resistor [tolerance=±5% resistance=220 package="2010 [SMD]"]

nets:
  N1: Part1.A5, POT3.PIN2
  N2: Part1.D21/SCL, S4.2, R3.Pin_1
  N3: Part1.GND, S4.4, POT3.PIN1, R1.Pin_0
  N4: Part1.D2_PWM, LED4.anode
  N5: LED4.cathode, R1.Pin_1
  N6: R3.Pin_0, POT3.PIN3
