# Fritzing sketch C6_InternetClock (saved by Fritzing 0.9.2b)
breadboards: 1
perfboards: 1

parts:
  Part1 = Arduino Mega 2560 (Rev3)
  LED4 = LED - 3mm [color="Green (555nm)" package="3 mm [THT]"]
  S4 = Momentary Switch [package=ksa_sealed_tac_switch]
  R3 = Resistor [tolerance=±5% resistance=10k package=THT]
  POT3 = Breadboard Trimpot
  LED8 = RGB LED (com. cathode, rgb) [color="Green (555nm)" package="5 mm [THT]"]
  U3 = 7-SEGMENT-4DIGIT [package=7-segment-4digit-5641]  # not connected
  U4 = 7-SEGMENT-4DIGIT [package=7-segment-4digit-5641]  # not connected
  R9 = PHOTOCELL [package=photocell]
  R10 = Resistor [tolerance=±5% resistance=10k package=THT]
  R7 = Resistor [tolerance=±5% resistance=220 package="2010 [SMD]"]
  R6 = Resistor [tolerance=±5% resistance=220 package="2010 [SMD]"]
  R8 = Resistor [tolerance=±5% resistance=220 package="2010 [SMD]"]
  R11 = Resistor [tolerance=±5% resistance=220 package="2010 [SMD]"]
  R1 = Resistor [tolerance=±5% resistance=220 package="2010 [SMD]"]

nets:
  N1: Part1.A8, R9.P$2, R10.Pin_0
  N2: Part1.A5, POT3.PIN2
  N3: Part1.D21/SCL, S4.2, R3.Pin_1
  N4: Part1.GND, S4.4, POT3.PIN1, R10.Pin_1, R1.Pin_0
  N5: Part1.5V, R3.Pin_0, POT3.PIN3, R9.P$1
  N6: Part1.D1_TX0, LED4.anode
  N7: Part1.D26, R11.Pin_1
  N8: Part1.D44, R8.Pin_0
  N9: Part1.D45, R7.Pin_0
  N10: Part1.D46, R6.Pin_0
  N11: LED4.cathode, R1.Pin_1
  N12: S4.3, LED8.common_cathode
  N13: LED8.red_anode, R8.Pin_1
  N14: LED8.green_anode, R7.Pin_1
  N15: LED8.blue_anode, R6.Pin_1

custom parts:
  7-SEGMENT-4DIGIT: if you need make parts, send me e-mail and write. Price 1 part=0.9 WMZ (http://www.wmtransfer.com/) ~ 0.9 Euro
