# Fritzing sketch C8_SocketLED (saved by Fritzing 0.9.2b)
breadboards: 1

parts:
  Part1 = Arduino Mega 2560 (Rev3)
  LED4 = LED - 3mm [color="Green (555nm)" package="3 mm [THT]"]
  S4 = Momentary Switch [package=ksa_sealed_tac_switch]
  R3 = Resistor [tolerance=±5% resistance=10k package=THT]
  LED8 = RGB LED (com. cathode, rgb) [color="Green (555nm)" package="5 mm [THT]"]
  CC3K1 = Adafruit CC3000 WiFi Breakout  # not connected
  R1 = Resistor [tolerance=±5% resistance=220 package="2010 [SMD]"]
  R8 = Resistor [tolerance=±5% resistance=220 package="2010 [SMD]"]
  R6 = Resistor [tolerance=±5% resistance=220 package="2010 [SMD]"]
  R7 = Resistor [tolerance=±5% resistance=220 package="2010 [SMD]"]

nets:
  N1: Part1.D21/SCL, S4.2, R3.Pin_1
  N2: Part1.GND, S4.4, R1.Pin_0
  N3: Part1.5V, R3.Pin_0
  N4: Part1.D2_PWM, LED4.anode
  N5: Part1.D44, R8.Pin_0
  N6: Part1.D45, R7.Pin_0
  N7: Part1.D46, R6.Pin_0
  N8: LED4.cathode, R1.Pin_1
  N9: S4.3, LED8.common_cathode
  N10: LED8.red_anode, R8.Pin_1
  N11: LED8.green_anode, R7.Pin_1
  N12: LED8.blue_anode, R6.Pin_1

custom parts:
  Adafruit CC3000 WiFi Breakout: CC3000 WiFi Breakout
