# Fritzing sketch C9_SocketsLCD16x2 (saved by Fritzing 0.9.2b)
breadboards: 1
perfboards: 1

parts:
  Part1 = Arduino Mega 2560 (Rev3)
  CC1 = Adafruit CC3000 Shield for Arduino
  LED3 = LED - 3mm [color="Yellow (595nm)" package="3 mm [THT]"]  # not connected
  LED4 = LED - 3mm [color="Green (555nm)" package="3 mm [THT]"]  # not connected
  LED5 = RGB LED (com. cathode, rgb) [color="Green (555nm)" package="5 mm [THT]"]  # not connected
  LCD1 = LCD screen
  LED2 = LED - 3mm [color="Red (635nm)" package="3 mm [THT]"]  # not connected
  Part2 = SRF05 Ultrasonic Rangefinder
  POT1 = Breadboard Trimpot
  R1 = Resistor [tolerance=±5% resistance=220 package="2010 [SMD]"]  # not connected
  R2 = Resistor [tolerance=±5% resistance=220 package="2010 [SMD]"]  # not connected
  R3 = Resistor [tolerance=±5% resistance=220 package="2010 [SMD]"]  # not connected

nets:
  N1: Part1.A10, Part2.VCC
  N2: Part1.A11, Part2.Trig
  N3: Part1.A12, Part2.Echo
  N4: Part1.A13, Part2.GND
  N5: Part1.A0, CC1.A0
  N6: Part1.A1, CC1.A1
  N7: Part1.A2, CC1.A2
  N8: Part1.A3, CC1.A3
  N9: Part1.A4, CC1.A4
  N10: Part1.A5, CC1.A5
  N11: Part1.D21/SCL, Part1.SCL, CC1.SCL
  N12: Part1.D20/SDA, Part1.SDA, CC1.SDA
  N13: Part1.D19/RX1, LCD1.RS
  N14: Part1.D18/TX1, LCD1.E
  N15: Part1.D17_PWM/RX2, LCD1.DB4
  N16: Part1.D16_PWM/TX2, LCD1.DB5
  N17: Part1.D15/RX3, LCD1.DB6
  N18: Part1.D14/TX3, LCD1.DB7
  N19: Part1.AREF, CC1.AREF
  GND: Part1.GND, CC1.GND, LCD1.VSS, LCD1.R/W, LCD1.LED-, POT1.PIN1
  N20: Part1.D13_PWM, CC1.D13
  N21: Part1.D12_PWM, CC1.D12
  N22: Part1.D11_PWM, CC1.D11
  N23: Part1.D10_PWM, CC1.D10
  N24: Part1.D9_PWM, CC1.D9
  N25: Part1.D8_PWM, CC1.D8
  N26: Part1.IOREF#254, CC1.NC
  N27: Part1.IOREF#255, CC1.IOr
  N28: Part1.RESET, CC1.RST
  N29: Part1.3V3, CC1.3V
  5V: Part1.5V, CC1.5V, LCD1.VDD, LCD1.LED+, POT1.PIN3
  VIN: Part1.VIN, CC1.VIN
  N30: Part1.D0_RX0, CC1.D0
  N31: Part1.D1_TX0, CC1.D1
  N32: Part1.D2_PWM, CC1.D2
  N33: Part1.D3_PWM, CC1.D3
  N34: Part1.D4_PWM, CC1.D4
  N35: Part1.D5_PWM, CC1.D5
  N36: Part1.D6_PWM, CC1.D6
  N37: Part1.D7_PWM, CC1.D7
  N38: LCD1.V0, POT1.PIN2
