# Fritzing sketch _CC3000BreakoutWiring2 (saved by Fritzing 0.9.1b)

parts:
  Part1 = Arduino Mega 2560 (Rev3)
  CC3K1 = Adafruit CC3000 WiFi Breakout

nets:
  N1: Part1.D10_PWM, CC3K1.CS
  N2: Part1.D3_PWM, CC3K1.IRQ
  N3: Part1.D5_PWM, CC3K1.VBEN

custom parts:
  Adafruit CC3000 WiFi Breakout: CC3000 WiFi Breakout
